// Logisim project Final.circ as structural Verilog: 21 circuits, main circuit ALU
module main (
  input  Sign_of_A,
  input  A3,
  input  A2,
  input  A1,
  input  A0,
  input  operation_Select,
  input  in_7,
  input  Sign_of_B,
  input  B3,
  input  B2,
  input  B1,
  input  B0,
  output Division_by_Zero,
  output Zero_flag,
  output Result_Sign
);

  wire alu_1_out_16, alu_1_out_17, alu_1_out_18, alu_1_out_19, alu_1_out_20, alu_1_out_21, alu_1_out_22,
       alu_1_out_23, binary_to_bcd_1_out_9, binary_to_bcd_1_out_10, binary_to_bcd_1_out_11,
       binary_to_bcd_1_out_12, binary_to_bcd_1_out_13, binary_to_bcd_1_out_14, binary_to_bcd_1_out_15,
       binary_to_bcd_1_out_16, binary_to_bcd_1_out_17, binary_to_bcd_1_out_18, n7se_1_a_2, n7se_1_b_2,
       n7se_1_c_2, n7se_1_d_2, n7se_1_e, n7se_1_f, n7se_1_g, n7se_2_a_2, n7se_2_b_2, n7se_2_c_2, n7se_2_d_2,
       n7se_2_e, n7se_2_f, n7se_2_g, n7se_3_a_2, n7se_3_b_2, n7se_3_c_2, n7se_3_d_2, n7se_3_e, n7se_3_f,
       n7se_3_g;

  ALU alu_1 (
    .in_6(operation_Select), .in_7(in_7), .in_1(Sign_of_A), .in_2(A3), .in_3(A2), .in_4(A1), .in_5(A0),
    .in_8(Sign_of_B), .in_9(B3), .in_10(B2), .in_11(B1), .in_12(B0), .out_13(Division_by_Zero),
    .out_14(Zero_flag), .out_15(Result_Sign), .out_16(alu_1_out_16), .out_17(alu_1_out_17),
    .out_18(alu_1_out_18), .out_19(alu_1_out_19), .out_20(alu_1_out_20), .out_21(alu_1_out_21),
    .out_22(alu_1_out_22), .out_23(alu_1_out_23));
  _7se u_7se_1 (
    .D(binary_to_bcd_1_out_17), .C(binary_to_bcd_1_out_18), .B(1'b0), .A(1'b0), .A_2(n7se_1_a_2),
    .b_2(n7se_1_b_2), .c_2(n7se_1_c_2), .d_2(n7se_1_d_2), .e(n7se_1_e), .f(n7se_1_f), .g(n7se_1_g));
  _7_Segment_Display u_7_segment_display_1 (
    .g(n7se_1_g), .f(n7se_1_f), .a(n7se_1_a_2), .b(n7se_1_b_2), .e(n7se_1_e), .d(n7se_1_d_2), .c(n7se_1_c_2));  // open: dp
  _7_Segment_Display u_7_segment_display_2 (
    .g(n7se_2_g), .f(n7se_2_f), .a(n7se_2_a_2), .b(n7se_2_b_2), .e(n7se_2_e), .d(n7se_2_d_2), .c(n7se_2_c_2));  // open: dp
  binary_to_bcd binary_to_bcd_1 (
    .A0(alu_1_out_23), .A1(alu_1_out_22), .A2(alu_1_out_21), .A3(alu_1_out_20), .A4(alu_1_out_19),
    .A5(alu_1_out_18), .A6(alu_1_out_17), .A7(alu_1_out_16), .out_9(binary_to_bcd_1_out_9),
    .out_10(binary_to_bcd_1_out_10), .out_11(binary_to_bcd_1_out_11), .out_12(binary_to_bcd_1_out_12),
    .out_13(binary_to_bcd_1_out_13), .out_14(binary_to_bcd_1_out_14), .out_15(binary_to_bcd_1_out_15),
    .out_16(binary_to_bcd_1_out_16), .out_17(binary_to_bcd_1_out_17), .out_18(binary_to_bcd_1_out_18));
  _7se u_7se_2 (
    .D(binary_to_bcd_1_out_13), .C(binary_to_bcd_1_out_14), .B(binary_to_bcd_1_out_15),
    .A(binary_to_bcd_1_out_16), .A_2(n7se_2_a_2), .b_2(n7se_2_b_2), .c_2(n7se_2_c_2), .d_2(n7se_2_d_2),
    .e(n7se_2_e), .f(n7se_2_f), .g(n7se_2_g));
  _7se u_7se_3 (
    .D(binary_to_bcd_1_out_9), .C(binary_to_bcd_1_out_10), .B(binary_to_bcd_1_out_11),
    .A(binary_to_bcd_1_out_12), .A_2(n7se_3_a_2), .b_2(n7se_3_b_2), .c_2(n7se_3_c_2), .d_2(n7se_3_d_2),
    .e(n7se_3_e), .f(n7se_3_f), .g(n7se_3_g));
  _7_Segment_Display u_7_segment_display_3 (
    .g(n7se_3_g), .f(n7se_3_f), .a(n7se_3_a_2), .b(n7se_3_b_2), .e(n7se_3_e), .d(n7se_3_d_2), .c(n7se_3_c_2));  // open: dp

  // Notes on the sheet:
  //   operation Select Guide
  //   00 for Addetion
  //   01 for Subtraction
  //   10 for Multiplication
  //   11 for Division
endmodule

module ALU (
  input  in_1,
  input  in_2,
  input  in_3,
  input  in_4,
  input  in_5,
  input  in_6,
  input  in_7,
  input  in_8,
  input  in_9,
  input  in_10,
  input  in_11,
  input  in_12,
  output out_13,
  output out_14,
  output out_15,
  output out_16,
  output out_17,
  output out_18,
  output out_19,
  output out_20,
  output out_21,
  output out_22,
  output out_23
);

  wire add_sub_1_r0, add_sub_1_r1, add_sub_1_r2, add_sub_1_r3, add_sub_1_r4, add_sub_1_sign_of_r,
       add_sub_1_zeroflag, and_1_out, and_2_out, and_3_out, and_4_out, and_4x1_1_out_6, and_4x1_1_out_7,
       and_4x1_1_out_8, and_4x1_1_out_9, and_4x1_2_out_6, and_4x1_2_out_7, and_4x1_2_out_8, and_4x1_2_out_9,
       and_4x1_3_out_6, and_4x1_4_out_6, and_4x1_4_out_7, and_4x1_4_out_8, and_4x1_4_out_9, and_5_out,
       and_6_out, and_7_out, and_8_out, and_9_out, and_10_out, and_12_out, and_13_out, multiplication_1_p0,
       multiplication_1_p1, multiplication_1_p2, multiplication_1_p3, multiplication_1_p4,
       multiplication_1_p5, multiplication_1_p6, multiplication_1_p7, multiplication_1_sign_flag,
       multiplication_1_zero_flag, n4_bit_x_4_bit_integer_signed_divider_1_out_11,
       n4_bit_x_4_bit_integer_signed_divider_1_q0, n4_bit_x_4_bit_integer_signed_divider_1_q1,
       n4_bit_x_4_bit_integer_signed_divider_1_q2, n4_bit_x_4_bit_integer_signed_divider_1_q3,
       n4_bit_x_4_bit_integer_signed_divider_1_sign_flag, n4_bit_x_4_bit_integer_signed_divider_1_zero_flag,
       not_1_out, not_2_out, or_1_out, or_2_out, or_3_out, or_4_out, or_5_out, or_6_out, or_7_out;

  not not_1 (not_1_out, in_6);
  not not_2 (not_2_out, in_7);
  and and_1 (and_1_out, not_1_out, not_2_out);
  and and_2 (and_2_out, not_1_out, in_7);
  and and_3 (and_3_out, in_6, not_2_out);
  and and_4 (and_4_out, in_6, in_7);
  or or_1 (or_1_out, and_1_out, and_2_out);
  and and_5 (and_5_out, in_7, or_1_out);
  and and_6 (and_6_out, or_1_out, add_sub_1_r0);
  Add_Sub add_sub_1 (
    .in_11(and_5_out), .Sign_of_A(in_1), .A3(in_2), .A2(in_3), .A1(in_4), .A0(in_5), .Sign_of_B(in_8),
    .B3(in_9), .B2(in_10), .B1(in_11), .B0(in_12), .ZeroFlag(add_sub_1_zeroflag),
    .Sign_of_R(add_sub_1_sign_of_r), .R4(add_sub_1_r4), .R3(add_sub_1_r3), .R2(add_sub_1_r2),
    .R1(add_sub_1_r1), .R0(add_sub_1_r0));
  AND_4x1 and_4x1_1 (
    .B(or_1_out), .A3(add_sub_1_r1), .A2(add_sub_1_r2), .A1(add_sub_1_r3), .A0(add_sub_1_r4),
    .out_6(and_4x1_1_out_6), .out_7(and_4x1_1_out_7), .out_8(and_4x1_1_out_8), .out_9(and_4x1_1_out_9));
  and and_7 (and_7_out, or_1_out, add_sub_1_zeroflag);
  and and_8 (and_8_out, or_1_out, add_sub_1_sign_of_r);
  Multiplication multiplication_1 (
    .in_1(in_1), .A3(in_2), .A2(in_3), .A1(in_4), .A0(in_5), .Sign_B(in_8), .B3(in_9), .B2(in_10),
    .B1(in_11), .B0(in_12), .Zero_Flag(multiplication_1_zero_flag), .Sign_Flag(multiplication_1_sign_flag),
    .P7(multiplication_1_p7), .P6(multiplication_1_p6), .P5(multiplication_1_p5), .P4(multiplication_1_p4),
    .P3(multiplication_1_p3), .P2(multiplication_1_p2), .P1(multiplication_1_p1), .P0(multiplication_1_p0));
  AND_4x1 and_4x1_2 (
    .B(and_3_out), .A3(multiplication_1_p0), .A2(multiplication_1_p1), .A1(multiplication_1_p2),
    .A0(multiplication_1_p3), .out_6(and_4x1_2_out_6), .out_7(and_4x1_2_out_7), .out_8(and_4x1_2_out_8),
    .out_9(and_4x1_2_out_9));
  and and_9 (and_9_out, and_3_out, multiplication_1_zero_flag);
  AND_4x1 and_4x1_3 (
    .B(and_3_out), .A3(multiplication_1_p4), .A2(multiplication_1_p5), .A1(multiplication_1_p6),
    .A0(multiplication_1_p7), .out_6(and_4x1_3_out_6), .out_7(out_18), .out_8(out_17), .out_9(out_16));
  _4_Bit_x_4_Bit_integer_signed_Divider u_4_bit_x_4_bit_integer_signed_divider_1 (
    .SIGN_A(in_1), .A3(in_2), .A2(in_3), .A1(in_4), .A0(in_5), .SIGN_B(in_8), .B3(in_9), .B2(in_10),
    .B1(in_11), .B0(in_12), .out_11(n4_bit_x_4_bit_integer_signed_divider_1_out_11),
    .ZERO_FLAG(n4_bit_x_4_bit_integer_signed_divider_1_zero_flag),
    .SIGN_FLAG(n4_bit_x_4_bit_integer_signed_divider_1_sign_flag),
    .Q3(n4_bit_x_4_bit_integer_signed_divider_1_q3), .Q2(n4_bit_x_4_bit_integer_signed_divider_1_q2),
    .Q1(n4_bit_x_4_bit_integer_signed_divider_1_q1), .Q0(n4_bit_x_4_bit_integer_signed_divider_1_q0));
  AND_4x1 and_4x1_4 (
    .B(and_4_out), .A3(n4_bit_x_4_bit_integer_signed_divider_1_q0),
    .A2(n4_bit_x_4_bit_integer_signed_divider_1_q1), .A1(n4_bit_x_4_bit_integer_signed_divider_1_q2),
    .A0(n4_bit_x_4_bit_integer_signed_divider_1_q3), .out_6(and_4x1_4_out_6), .out_7(and_4x1_4_out_7),
    .out_8(and_4x1_4_out_8), .out_9(and_4x1_4_out_9));
  and and_10 (and_10_out, and_4_out, n4_bit_x_4_bit_integer_signed_divider_1_zero_flag);
  and and_11 (out_13, n4_bit_x_4_bit_integer_signed_divider_1_out_11, and_4_out);
  and and_12 (and_12_out, and_3_out, multiplication_1_sign_flag);
  and and_13 (and_13_out, and_4_out, n4_bit_x_4_bit_integer_signed_divider_1_sign_flag);
  or or_2 (or_2_out, and_12_out, and_8_out);
  or or_3 (or_3_out, and_4x1_4_out_9, and_4x1_2_out_9);
  or or_4 (or_4_out, and_4x1_2_out_8, and_4x1_1_out_7);
  or or_5 (or_5_out, and_4x1_4_out_7, and_4x1_2_out_7);
  or or_6 (or_6_out, and_4x1_4_out_6, and_4x1_2_out_6);
  or or_7 (or_7_out, and_10_out, and_9_out);
  or or_8 (out_19, and_4x1_3_out_6, and_4x1_1_out_9);
  or or_9 (out_20, or_3_out, and_4x1_1_out_8);
  or or_10 (out_21, or_4_out, and_4x1_4_out_8);
  or or_11 (out_14, or_7_out, and_7_out);
  or or_12 (out_15, or_2_out, and_13_out);
  or or_13 (out_22, or_5_out, and_4x1_1_out_6);
  or or_14 (out_23, or_6_out, and_6_out);
endmodule

module FullAdder (
  input  A1,
  input  B1,
  input  in_3,
  output out_4,
  output out_5
);

  wire and_1_out, and_2_out, xor_1_out;

  xor xor_1 (xor_1_out, A1, B1);
  and and_1 (and_1_out, A1, B1);
  and and_2 (and_2_out, xor_1_out, in_3);
  xor xor_2 (out_4, xor_1_out, in_3);
  or or_1 (out_5, and_1_out, and_2_out);
endmodule

module OPERATIONDECIDER (
  input  A,
  input  B,
  input  M,
  output operation
);

  wire and_1_out, and_2_out, not_1_out, xnor_1_out, xor_1_out;

  not not_1 (not_1_out, A);
  xor xor_1 (xor_1_out, B, M);
  xnor xnor_1 (xnor_1_out, B, M);
  and and_1 (and_1_out, not_1_out, xor_1_out);
  and and_2 (and_2_out, A, xnor_1_out);
  or or_1 (operation, and_1_out, and_2_out);
endmodule

module COMPARATOR (
  input  Sin,
  input  A,
  input  B,
  output A_B,
  output B_A,
  output Sout
);

  wire not_1_out, not_2_out, xnor_1_out;

  not not_1 (not_1_out, A);
  not not_2 (not_2_out, B);
  and and_1 (A_B, Sin, not_2_out, A);
  and and_2 (B_A, Sin, not_1_out, B);
  xnor xnor_1 (xnor_1_out, A, B);
  and and_3 (Sout, Sin, xnor_1_out);
endmodule

module _4BITCOMPARATOR (
  input  in_1,
  input  in_2,
  input  in_3,
  input  in_4,
  input  in_5,
  input  in_6,
  input  in_7,
  input  in_8,
  output out_9,
  output A___B___0,
  output A_B,
  output B_A
);

  wire and_1_out, and_2_out, and_3_out, comparator_1_a_b, comparator_1_b_a, comparator_1_sout,
       comparator_2_a_b, comparator_2_b_a, comparator_2_sout, comparator_3_a_b, comparator_3_b_a,
       comparator_3_sout, comparator_4_a_b, comparator_4_b_a, nor_1_out, nor_2_out, nor_3_out, nor_4_out,
       or_1_out, or_2_out, or_3_out, or_4_out;

  COMPARATOR comparator_1 (
    .Sin(1'b1), .A(in_1), .B(in_5), .A_B(comparator_1_a_b), .B_A(comparator_1_b_a), .Sout(comparator_1_sout));
  COMPARATOR comparator_2 (
    .Sin(comparator_1_sout), .A(in_2), .B(in_6), .A_B(comparator_2_a_b), .B_A(comparator_2_b_a),
    .Sout(comparator_2_sout));
  COMPARATOR comparator_3 (
    .Sin(comparator_2_sout), .A(in_3), .B(in_7), .A_B(comparator_3_a_b), .B_A(comparator_3_b_a),
    .Sout(comparator_3_sout));
  COMPARATOR comparator_4 (
    .Sin(comparator_3_sout), .A(in_4), .B(in_8), .A_B(comparator_4_a_b), .B_A(comparator_4_b_a), .Sout(out_9));
  nor nor_1 (nor_1_out, in_4, in_8);
  nor nor_2 (nor_2_out, in_3, in_7);
  nor nor_3 (nor_3_out, in_2, in_6);
  nor nor_4 (nor_4_out, in_1, in_5);
  or or_1 (or_1_out, comparator_4_a_b, comparator_3_a_b);
  or or_2 (or_2_out, comparator_2_a_b, comparator_1_a_b);
  or or_3 (or_3_out, comparator_4_b_a, comparator_3_b_a);
  or or_4 (or_4_out, comparator_2_b_a, comparator_1_b_a);
  and and_1 (and_1_out, out_9, nor_1_out);
  and and_2 (and_2_out, nor_2_out, nor_3_out);
  or or_5 (A_B, or_1_out, or_2_out);
  or or_6 (B_A, or_3_out, or_4_out);
  and and_3 (and_3_out, and_2_out, nor_4_out);
  and and_4 (A___B___0, and_1_out, and_3_out);

  // Notes on the sheet:
  //   A=B
endmodule

module SIGNHANDLER (
  input  A___B,
  input  A,
  input  operation,
  output out_4
);

  wire and_1_out, and_2_out, not_1_out, xnor_1_out;

  not not_1 (not_1_out, operation);
  xnor xnor_1 (xnor_1_out, A___B, A);
  and and_1 (and_1_out, A, not_1_out);
  and and_2 (and_2_out, xnor_1_out, operation);
  or or_1 (out_4, and_2_out, and_1_out);
endmodule

module shift_add_3 (
  input  A0,
  input  A1,
  input  A2,
  input  A3,
  output out_5,
  output out_6,
  output out_7,
  output out_8
);

  wire and_1_out, and_2_out, and_3_out, and_4_out, and_5_out, and_6_out, and_7_out, and_8_out, and_9_out,
       and_10_out, not_1_out, not_2_out, not_3_out, not_4_out, or_1_out, or_2_out, or_3_out;

  not not_1 (not_1_out, A3);
  not not_2 (not_2_out, A1);
  not not_3 (not_3_out, A2);
  not not_4 (not_4_out, A0);
  and and_1 (and_1_out, A1, A2);
  and and_2 (and_2_out, A0, not_3_out);
  or or_1 (or_1_out, not_3_out, A0);
  or or_2 (or_2_out, A1, A0);
  or or_3 (or_3_out, A3, and_1_out);
  and and_3 (and_3_out, and_2_out, not_1_out);
  and and_4 (and_4_out, not_4_out, or_3_out);
  and and_5 (and_5_out, or_1_out, A1);
  and and_6 (and_6_out, not_4_out, A3);
  and and_7 (and_7_out, A3, A0);
  and and_8 (and_8_out, A2, not_2_out);
  and and_9 (and_9_out, or_2_out, A2);
  and and_10 (and_10_out, and_8_out, not_4_out);
  or or_4 (out_5, and_4_out, and_3_out);
  or or_5 (out_6, and_5_out, and_6_out);
  or or_6 (out_7, and_7_out, and_10_out);
  or or_7 (out_8, A3, and_9_out);
endmodule

module binary_to_bcd (
  input  A0,
  input  A1,
  input  A2,
  input  A3,
  input  A4,
  input  A5,
  input  A6,
  input  A7,
  output out_9,
  output out_10,
  output out_11,
  output out_12,
  output out_13,
  output out_14,
  output out_15,
  output out_16,
  output out_17,
  output out_18
);

  wire shift_add_3_1_out_5, shift_add_3_1_out_6, shift_add_3_1_out_7, shift_add_3_1_out_8,
       shift_add_3_2_out_5, shift_add_3_2_out_6, shift_add_3_2_out_7, shift_add_3_2_out_8,
       shift_add_3_3_out_5, shift_add_3_3_out_6, shift_add_3_3_out_7, shift_add_3_5_out_5,
       shift_add_3_5_out_6, shift_add_3_5_out_7, shift_add_3_5_out_8, shift_add_3_6_out_5,
       shift_add_3_6_out_6, shift_add_3_6_out_7, shift_add_3_6_out_8;

  shift_add_3 shift_add_3_1 (
    .A0(A5), .A1(A6), .A2(A7), .A3(1'b0), .out_5(shift_add_3_1_out_5), .out_6(shift_add_3_1_out_6),
    .out_7(shift_add_3_1_out_7), .out_8(shift_add_3_1_out_8));
  shift_add_3 shift_add_3_2 (
    .A0(A4), .A1(shift_add_3_1_out_5), .A2(shift_add_3_1_out_6), .A3(shift_add_3_1_out_7),
    .out_5(shift_add_3_2_out_5), .out_6(shift_add_3_2_out_6), .out_7(shift_add_3_2_out_7),
    .out_8(shift_add_3_2_out_8));
  shift_add_3 shift_add_3_3 (
    .A0(shift_add_3_5_out_8), .A1(shift_add_3_2_out_8), .A2(shift_add_3_1_out_8), .A3(1'b0),
    .out_5(shift_add_3_3_out_5), .out_6(shift_add_3_3_out_6), .out_7(shift_add_3_3_out_7), .out_8(out_18));
  shift_add_3 shift_add_3_4 (
    .A0(shift_add_3_6_out_8), .A1(shift_add_3_3_out_5), .A2(shift_add_3_3_out_6), .A3(shift_add_3_3_out_7),
    .out_5(out_14), .out_6(out_15), .out_7(out_16), .out_8(out_17));
  shift_add_3 shift_add_3_5 (
    .A0(A3), .A1(shift_add_3_2_out_5), .A2(shift_add_3_2_out_6), .A3(shift_add_3_2_out_7),
    .out_5(shift_add_3_5_out_5), .out_6(shift_add_3_5_out_6), .out_7(shift_add_3_5_out_7),
    .out_8(shift_add_3_5_out_8));
  shift_add_3 shift_add_3_6 (
    .A0(A2), .A1(shift_add_3_5_out_5), .A2(shift_add_3_5_out_6), .A3(shift_add_3_5_out_7),
    .out_5(shift_add_3_6_out_5), .out_6(shift_add_3_6_out_6), .out_7(shift_add_3_6_out_7),
    .out_8(shift_add_3_6_out_8));
  shift_add_3 shift_add_3_7 (
    .A0(A1), .A1(shift_add_3_6_out_5), .A2(shift_add_3_6_out_6), .A3(shift_add_3_6_out_7), .out_5(out_10),
    .out_6(out_11), .out_7(out_12), .out_8(out_13));

  assign out_9 = A0;

  // Notes on the sheet:
  //   0
endmodule

module _7se (
  input  D,
  input  C,
  input  B,
  input  A,
  output A_2,
  output b_2,
  output c_2,
  output d_2,
  output e,
  output f,
  output g
);

  wire and_1_out, and_2_out, and_3_out, and_4_out, and_5_out, and_6_out, and_7_out, and_8_out, and_9_out,
       not_1_out, not_2_out, not_3_out, not_4_out;

  not not_1 (not_1_out, A);
  not not_2 (not_2_out, B);
  not not_3 (not_3_out, C);
  not not_4 (not_4_out, D);
  and and_1 (and_1_out, B, not_3_out);
  and and_2 (and_2_out, B, not_4_out);
  and and_3 (and_3_out, B, D);
  and and_4 (and_4_out, not_2_out, not_4_out);
  and and_5 (and_5_out, C, D);
  and and_6 (and_6_out, not_3_out, not_4_out);
  or or_1 (c_2, B, not_3_out, D);
  and and_7 (and_7_out, C, not_4_out);
  and and_8 (and_8_out, not_2_out, C);
  and and_9 (and_9_out, D, and_1_out);
  or or_2 (A_2, and_3_out, and_4_out, A, C);
  or or_3 (b_2, and_5_out, and_6_out, not_2_out);
  or or_4 (d_2, A, and_4_out, and_7_out, and_8_out, and_9_out);
  or or_5 (e, and_7_out, and_4_out);
  or or_6 (f, A, and_6_out, and_2_out, and_1_out);
  or or_7 (g, A, and_1_out, and_8_out, and_7_out);

  // Notes on the sheet:
  //   a
endmodule

module BCDTO7SE (
  input  in_1,
  input  in_2,
  input  in_3,
  input  in_4,
  input  in_5,
  input  in_6,
  input  in_7,
  input  in_8
);

  wire binary_to_bcd_1_out_9, binary_to_bcd_1_out_10, binary_to_bcd_1_out_11, binary_to_bcd_1_out_12,
       binary_to_bcd_1_out_13, binary_to_bcd_1_out_14, binary_to_bcd_1_out_15, binary_to_bcd_1_out_16,
       binary_to_bcd_1_out_17, binary_to_bcd_1_out_18, n7se_1_a_2, n7se_1_b_2, n7se_1_c_2, n7se_1_d_2,
       n7se_1_e, n7se_1_f, n7se_1_g, n7se_2_a_2, n7se_2_b_2, n7se_2_c_2, n7se_2_d_2, n7se_2_e, n7se_2_f,
       n7se_2_g, n7se_3_a_2, n7se_3_b_2, n7se_3_c_2, n7se_3_d_2, n7se_3_e, n7se_3_f, n7se_3_g;

  _7_Segment_Display u_7_segment_display_1 (
    .g(n7se_1_g), .f(n7se_1_f), .a(n7se_1_a_2), .b(n7se_1_b_2), .e(n7se_1_e), .d(n7se_1_d_2), .c(n7se_1_c_2));  // open: dp
  _7se u_7se_1 (
    .D(binary_to_bcd_1_out_17), .C(binary_to_bcd_1_out_18), .B(1'b0), .A(1'b0), .A_2(n7se_1_a_2),
    .b_2(n7se_1_b_2), .c_2(n7se_1_c_2), .d_2(n7se_1_d_2), .e(n7se_1_e), .f(n7se_1_f), .g(n7se_1_g));
  _7_Segment_Display u_7_segment_display_2 (
    .g(n7se_2_g), .f(n7se_2_f), .a(n7se_2_a_2), .b(n7se_2_b_2), .e(n7se_2_e), .d(n7se_2_d_2), .c(n7se_2_c_2));  // open: dp
  binary_to_bcd binary_to_bcd_1 (
    .A0(in_8), .A1(in_7), .A2(in_6), .A3(in_5), .A4(in_4), .A5(in_3), .A6(in_2), .A7(in_1),
    .out_9(binary_to_bcd_1_out_9), .out_10(binary_to_bcd_1_out_10), .out_11(binary_to_bcd_1_out_11),
    .out_12(binary_to_bcd_1_out_12), .out_13(binary_to_bcd_1_out_13), .out_14(binary_to_bcd_1_out_14),
    .out_15(binary_to_bcd_1_out_15), .out_16(binary_to_bcd_1_out_16), .out_17(binary_to_bcd_1_out_17),
    .out_18(binary_to_bcd_1_out_18));
  _7se u_7se_2 (
    .D(binary_to_bcd_1_out_13), .C(binary_to_bcd_1_out_14), .B(binary_to_bcd_1_out_15),
    .A(binary_to_bcd_1_out_16), .A_2(n7se_2_a_2), .b_2(n7se_2_b_2), .c_2(n7se_2_c_2), .d_2(n7se_2_d_2),
    .e(n7se_2_e), .f(n7se_2_f), .g(n7se_2_g));
  _7se u_7se_3 (
    .D(binary_to_bcd_1_out_9), .C(binary_to_bcd_1_out_10), .B(binary_to_bcd_1_out_11),
    .A(binary_to_bcd_1_out_12), .A_2(n7se_3_a_2), .b_2(n7se_3_b_2), .c_2(n7se_3_c_2), .d_2(n7se_3_d_2),
    .e(n7se_3_e), .f(n7se_3_f), .g(n7se_3_g));
  _7_Segment_Display u_7_segment_display_3 (
    .g(n7se_3_g), .f(n7se_3_f), .a(n7se_3_a_2), .b(n7se_3_b_2), .e(n7se_3_e), .d(n7se_3_d_2), .c(n7se_3_c_2));  // open: dp
endmodule

module Add_Sub (
  input  Sign_of_A,
  input  A3,
  input  A2,
  input  A1,
  input  A0,
  input  B2,
  input  B1,
  input  B0,
  input  Sign_of_B,
  input  B3,
  input  in_11,
  output ZeroFlag,
  output Sign_of_R,
  output R4,
  output R3,
  output R2,
  output R1,
  output R0
);

  wire and_5_out, and_6_out, and_8_out, fulladder_1_out_4, fulladder_1_out_5, fulladder_2_out_4,
       fulladder_2_out_5, fulladder_3_out_4, fulladder_3_out_5, fulladder_4_out_4, fulladder_4_out_5,
       n4bitcomparator_1_a___b___0, n4bitcomparator_1_a_b, n4bitcomparator_1_b_a, n4bitcomparator_1_out_9,
       not_1_out, operationdecider_1_operation, signhandler_1_out_4, xor_1_out, xor_2_out, xor_3_out,
       xor_4_out, xor_5_out, xor_6_out, xor_7_out, xor_8_out, xor_9_out;

  OPERATIONDECIDER operationdecider_1 (
    .A(in_11), .B(Sign_of_A), .M(Sign_of_B), .operation(operationdecider_1_operation));
  xor xor_1 (xor_1_out, B3, and_6_out);
  xor xor_2 (xor_2_out, operationdecider_1_operation, fulladder_1_out_5);
  xor xor_3 (xor_3_out, A3, and_5_out);
  xor xor_4 (xor_4_out, B2, and_6_out);
  FullAdder fulladder_1 (
    .A1(xor_3_out), .B1(xor_1_out), .in_3(fulladder_2_out_5), .out_4(fulladder_1_out_4),
    .out_5(fulladder_1_out_5));
  and and_1 (R4, xor_2_out, not_1_out);
  xor xor_5 (xor_5_out, A2, and_5_out);
  xor xor_6 (xor_6_out, B1, and_6_out);
  FullAdder fulladder_2 (
    .A1(xor_5_out), .B1(xor_4_out), .in_3(fulladder_3_out_5), .out_4(fulladder_2_out_4),
    .out_5(fulladder_2_out_5));
  and and_2 (R3, fulladder_1_out_4, not_1_out);
  xor xor_7 (xor_7_out, A1, and_5_out);
  and and_3 (R2, fulladder_2_out_4, not_1_out);
  xor xor_8 (xor_8_out, A0, and_5_out);
  xor xor_9 (xor_9_out, B0, and_6_out);
  FullAdder fulladder_3 (
    .A1(xor_7_out), .B1(xor_6_out), .in_3(fulladder_4_out_5), .out_4(fulladder_3_out_4),
    .out_5(fulladder_3_out_5));
  and and_4 (R1, fulladder_3_out_4, not_1_out);
  and and_5 (and_5_out, n4bitcomparator_1_b_a, operationdecider_1_operation);
  and and_6 (and_6_out, n4bitcomparator_1_a_b, operationdecider_1_operation);
  FullAdder fulladder_4 (
    .A1(xor_8_out), .B1(xor_9_out), .in_3(operationdecider_1_operation), .out_4(fulladder_4_out_4),
    .out_5(fulladder_4_out_5));
  and and_7 (R0, fulladder_4_out_4, not_1_out);
  not not_1 (not_1_out, ZeroFlag);
  _4BITCOMPARATOR u_4bitcomparator_1 (
    .in_1(A3), .in_2(A2), .in_3(A1), .in_4(A0), .in_5(B3), .in_6(B2), .in_7(B1), .in_8(B0),
    .out_9(n4bitcomparator_1_out_9), .A___B___0(n4bitcomparator_1_a___b___0), .A_B(n4bitcomparator_1_a_b),
    .B_A(n4bitcomparator_1_b_a));
  SIGNHANDLER signhandler_1 (
    .operation(operationdecider_1_operation), .A___B(and_6_out), .A(Sign_of_A), .out_4(signhandler_1_out_4));
  and and_8 (and_8_out, operationdecider_1_operation, n4bitcomparator_1_out_9);
  or or_1 (ZeroFlag, and_8_out, n4bitcomparator_1_a___b___0);
  and and_9 (Sign_of_R, not_1_out, signhandler_1_out_4);

  // Notes on the sheet:
  //   OPERATIONDECIDER
  //   FullAdders
  //   ZeroCheck
  //   COMPARATOR
  //   SIGNHANDLER
endmodule

module AND_4x1 (
  input  B,
  input  A3,
  input  A2,
  input  A1,
  input  A0,
  output out_6,
  output out_7,
  output out_8,
  output out_9
);

  and and_1 (out_6, B, A3);
  and and_2 (out_7, B, A2);
  and and_3 (out_8, B, A1);
  and and_4 (out_9, B, A0);
endmodule

module Full_Adder_4x4_Input (
  input  Cin,
  input  A0,
  input  A1,
  input  A2,
  input  A3,
  input  B0,
  input  B1,
  input  B2,
  input  B3,
  output S1,
  output S2,
  output S3,
  output S4,
  output Cout
);

  wire fulladder_1_out_5, fulladder_2_out_5, fulladder_3_out_5;

  FullAdder fulladder_1 (.A1(Cin), .B1(A0), .in_3(B0), .out_4(S1), .out_5(fulladder_1_out_5));
  FullAdder fulladder_2 (.A1(fulladder_1_out_5), .B1(A1), .in_3(B1), .out_4(S2), .out_5(fulladder_2_out_5));
  FullAdder fulladder_3 (.A1(fulladder_2_out_5), .B1(A2), .in_3(B2), .out_4(S3), .out_5(fulladder_3_out_5));
  FullAdder fulladder_4 (.A1(fulladder_3_out_5), .B1(A3), .in_3(B3), .out_4(S4), .out_5(Cout));
endmodule

module Multiplication (
  input  in_1,
  input  A3,
  input  A2,
  input  A1,
  input  A0,
  input  B2,
  input  B1,
  input  B0,
  input  Sign_B,
  input  B3,
  output Zero_Flag,
  output Sign_Flag,
  output P7,
  output P6,
  output P5,
  output P4,
  output P3,
  output P2,
  output P1,
  output P0
);

  wire and_4x1_1_out_6, and_4x1_1_out_7, and_4x1_1_out_8, and_4x1_1_out_9, and_4x1_2_out_6, and_4x1_2_out_7,
       and_4x1_2_out_8, and_4x1_2_out_9, and_4x1_3_out_6, and_4x1_3_out_7, and_4x1_3_out_8, and_4x1_3_out_9,
       and_4x1_4_out_6, and_4x1_4_out_7, and_4x1_4_out_8, full_adder_4x4_input_2_cout,
       full_adder_4x4_input_2_s2, full_adder_4x4_input_2_s3, full_adder_4x4_input_2_s4,
       full_adder_4x4_input_3_cout, full_adder_4x4_input_3_s2, full_adder_4x4_input_3_s3,
       full_adder_4x4_input_3_s4, nor_1_out, nor_2_out;

  xor xor_1 (Sign_Flag, Sign_B, in_1);
  AND_4x1 and_4x1_1 (
    .B(B3), .A3(A3), .A2(A2), .A1(A1), .A0(A0), .out_6(and_4x1_1_out_6), .out_7(and_4x1_1_out_7),
    .out_8(and_4x1_1_out_8), .out_9(and_4x1_1_out_9));
  Full_Adder_4x4_Input full_adder_4x4_input_1 (
    .Cin(1'b0), .A0(full_adder_4x4_input_2_s2), .A1(full_adder_4x4_input_2_s3),
    .A2(full_adder_4x4_input_2_s4), .A3(full_adder_4x4_input_2_cout), .B0(and_4x1_1_out_9),
    .B1(and_4x1_1_out_8), .B2(and_4x1_1_out_7), .B3(and_4x1_1_out_6), .S1(P3), .S2(P4), .S3(P5), .S4(P6),
    .Cout(P7));
  AND_4x1 and_4x1_2 (
    .B(B2), .A3(A3), .A2(A2), .A1(A1), .A0(A0), .out_6(and_4x1_2_out_6), .out_7(and_4x1_2_out_7),
    .out_8(and_4x1_2_out_8), .out_9(and_4x1_2_out_9));
  Full_Adder_4x4_Input full_adder_4x4_input_2 (
    .Cin(1'b0), .A0(full_adder_4x4_input_3_s2), .A1(full_adder_4x4_input_3_s3),
    .A2(full_adder_4x4_input_3_s4), .A3(full_adder_4x4_input_3_cout), .B0(and_4x1_2_out_9),
    .B1(and_4x1_2_out_8), .B2(and_4x1_2_out_7), .B3(and_4x1_2_out_6), .S1(P2),
    .S2(full_adder_4x4_input_2_s2), .S3(full_adder_4x4_input_2_s3), .S4(full_adder_4x4_input_2_s4),
    .Cout(full_adder_4x4_input_2_cout));
  AND_4x1 and_4x1_3 (
    .B(B1), .A3(A3), .A2(A2), .A1(A1), .A0(A0), .out_6(and_4x1_3_out_6), .out_7(and_4x1_3_out_7),
    .out_8(and_4x1_3_out_8), .out_9(and_4x1_3_out_9));
  Full_Adder_4x4_Input full_adder_4x4_input_3 (
    .Cin(1'b0), .A0(and_4x1_4_out_8), .A1(and_4x1_4_out_7), .A2(and_4x1_4_out_6), .A3(1'b0),
    .B0(and_4x1_3_out_9), .B1(and_4x1_3_out_8), .B2(and_4x1_3_out_7), .B3(and_4x1_3_out_6), .S1(P1),
    .S2(full_adder_4x4_input_3_s2), .S3(full_adder_4x4_input_3_s3), .S4(full_adder_4x4_input_3_s4),
    .Cout(full_adder_4x4_input_3_cout));
  AND_4x1 and_4x1_4 (
    .B(B0), .A3(A3), .A2(A2), .A1(A1), .A0(A0), .out_6(and_4x1_4_out_6), .out_7(and_4x1_4_out_7),
    .out_8(and_4x1_4_out_8), .out_9(P0));
  nor nor_1 (nor_1_out, B3, B2, B1, B0);
  nor nor_2 (nor_2_out, A3, A2, A1, A0);
  or or_1 (Zero_Flag, nor_1_out, nor_2_out);

  // Notes on the sheet:
  //   Sign-A
endmodule

module _4_Bit_Binary_Adder (
  input  C0,
  input  A2,
  input  B2,
  input  A0,
  input  B0,
  input  A3,
  input  B3,
  input  A1,
  input  B1,
  output C4,
  output S3,
  output S2,
  output S1,
  output S0
);

  wire fulladder_2_out_5, fulladder_3_out_5, fulladder_4_out_5;

  FullAdder fulladder_1 (.A1(A3), .B1(B3), .in_3(fulladder_2_out_5), .out_4(S3), .out_5(C4));
  FullAdder fulladder_2 (.A1(A2), .B1(B2), .in_3(fulladder_3_out_5), .out_4(S2), .out_5(fulladder_2_out_5));
  FullAdder fulladder_3 (.A1(A1), .B1(B1), .in_3(fulladder_4_out_5), .out_4(S1), .out_5(fulladder_3_out_5));
  FullAdder fulladder_4 (.A1(A0), .B1(B0), .in_3(C0), .out_4(S0), .out_5(fulladder_4_out_5));

  // Notes on the sheet:
  //   C3
  //   C2
  //   C1
endmodule

module _4_Bit_Binary_Subtractor (
  input  in_1,
  input  in_2,
  input  in_3,
  input  in_4,
  input  in_5,
  input  in_6,
  input  in_7,
  input  in_8,
  input  in_9,
  output out_10,
  output out_11,
  output out_12,
  output out_13
);

  wire n4_bit_binary_adder_1_c4, not_1_out, not_2_out, not_3_out, not_4_out;

  not not_1 (not_1_out, in_8);
  not not_2 (not_2_out, in_6);
  _4_Bit_Binary_Adder u_4_bit_binary_adder_1 (
    .C4(n4_bit_binary_adder_1_c4), .S3(out_10), .A3(in_9), .B3(not_1_out), .S2(out_11), .A2(in_7),
    .B2(not_2_out), .S1(out_12), .A1(in_5), .B1(not_4_out), .S0(out_13), .A0(in_2), .B0(not_3_out), .C0(in_1));
  not not_3 (not_3_out, in_3);
  not not_4 (not_4_out, in_4);
endmodule

module DEMUX (
  input  in_1,
  input  in_2,
  input  in_3,
  input  in_4,
  input  in_5,
  output out_6,
  output out_7,
  output out_8,
  output out_9
);

  and and_1 (out_6, in_1, in_5);
  and and_2 (out_7, in_2, in_5);
  and and_3 (out_8, in_3, in_5);
  and and_4 (out_9, in_4, in_5);
endmodule

module _4_Bit_x_4_Bit_integer_signed_Divider (
  input  SIGN_B,
  input  B3,
  input  B2,
  input  B1,
  input  B0,
  input  SIGN_A,
  input  A3,
  input  A2,
  input  A1,
  input  A0,
  output out_11,
  output ZERO_FLAG,
  output SIGN_FLAG,
  output Q3,
  output Q2,
  output Q1,
  output Q0
);

  wire demux_1_out_6, demux_1_out_7, demux_1_out_8, demux_1_out_9, demux_2_out_6, demux_2_out_7,
       demux_2_out_8, demux_2_out_9, demux_3_out_6, demux_3_out_7, demux_3_out_8, demux_3_out_9,
       n4_bit_binary_subtractor_1_out_10, n4_bit_binary_subtractor_1_out_11,
       n4_bit_binary_subtractor_1_out_12, n4_bit_binary_subtractor_1_out_13,
       n4_bit_binary_subtractor_2_out_10, n4_bit_binary_subtractor_2_out_11,
       n4_bit_binary_subtractor_2_out_12, n4_bit_binary_subtractor_2_out_13,
       n4_bit_binary_subtractor_3_out_10, n4_bit_binary_subtractor_3_out_11,
       n4_bit_binary_subtractor_3_out_12, n4_bit_binary_subtractor_3_out_13,
       n4_bit_x_4_bit_comparator_1_out_11, n4_bit_x_4_bit_comparator_2_out_11,
       n4_bit_x_4_bit_comparator_3_out_11, n4_bit_x_4_bit_comparator_4_out_11, not_1_out;

  xor xor_1 (SIGN_FLAG, SIGN_A, SIGN_B);
  nor nor_1 (ZERO_FLAG, Q3, Q2, Q1, Q0);
  nor nor_2 (out_11, B0, B1, B2, B3);
  not not_1 (not_1_out, 1'b0);
  _4_Bit_x_4_Bit_Comparator u_4_bit_x_4_bit_comparator_1 (
    .in_1(A3), .in_2(1'b0), .in_3(1'b0), .in_4(1'b0), .in_5(B0), .in_6(B1), .in_7(B2), .in_8(B3),
    .out_11(n4_bit_x_4_bit_comparator_1_out_11));  // open: out_9, out_10
  DEMUX demux_1 (
    .in_1(B3), .in_2(B2), .in_3(B1), .in_4(B0), .out_6(demux_1_out_6), .out_7(demux_1_out_7),
    .out_8(demux_1_out_8), .out_9(demux_1_out_9), .in_5(Q1));
  not not_2 (Q3, n4_bit_x_4_bit_comparator_1_out_11);
  DEMUX demux_2 (
    .in_1(B3), .in_2(B2), .in_3(B1), .in_4(B0), .out_6(demux_2_out_6), .out_7(demux_2_out_7),
    .out_8(demux_2_out_8), .out_9(demux_2_out_9), .in_5(Q3));
  DEMUX demux_3 (
    .in_1(B3), .in_2(B2), .in_3(B1), .in_4(B0), .out_6(demux_3_out_6), .out_7(demux_3_out_7),
    .out_8(demux_3_out_8), .out_9(demux_3_out_9), .in_5(Q2));
  _4_Bit_x_4_Bit_Comparator u_4_bit_x_4_bit_comparator_2 (
    .in_1(A0), .in_2(n4_bit_binary_subtractor_1_out_13), .in_3(n4_bit_binary_subtractor_1_out_12),
    .in_4(n4_bit_binary_subtractor_1_out_11), .in_5(B0), .in_6(B1), .in_7(B2), .in_8(B3),
    .out_11(n4_bit_x_4_bit_comparator_2_out_11));  // open: out_9, out_10
  _4_Bit_Binary_Subtractor u_4_bit_binary_subtractor_1 (
    .out_10(n4_bit_binary_subtractor_1_out_10), .out_11(n4_bit_binary_subtractor_1_out_11),
    .out_12(n4_bit_binary_subtractor_1_out_12), .out_13(n4_bit_binary_subtractor_1_out_13),
    .in_9(n4_bit_binary_subtractor_3_out_11), .in_8(demux_1_out_6), .in_7(n4_bit_binary_subtractor_3_out_12),
    .in_6(demux_1_out_7), .in_5(n4_bit_binary_subtractor_3_out_13), .in_4(demux_1_out_8), .in_2(A1),
    .in_3(demux_1_out_9), .in_1(not_1_out));
  _4_Bit_x_4_Bit_Comparator u_4_bit_x_4_bit_comparator_3 (
    .in_1(A1), .in_2(n4_bit_binary_subtractor_3_out_13), .in_3(n4_bit_binary_subtractor_3_out_12),
    .in_4(n4_bit_binary_subtractor_3_out_11), .in_5(B0), .in_6(B1), .in_7(B2), .in_8(B3),
    .out_11(n4_bit_x_4_bit_comparator_3_out_11));  // open: out_9, out_10
  not not_3 (Q0, n4_bit_x_4_bit_comparator_2_out_11);
  _4_Bit_Binary_Subtractor u_4_bit_binary_subtractor_2 (
    .out_10(n4_bit_binary_subtractor_2_out_10), .out_11(n4_bit_binary_subtractor_2_out_11),
    .out_12(n4_bit_binary_subtractor_2_out_12), .out_13(n4_bit_binary_subtractor_2_out_13), .in_9(1'b0),
    .in_8(demux_2_out_6), .in_7(1'b0), .in_6(demux_2_out_7), .in_5(1'b0), .in_4(demux_2_out_8), .in_2(A3),
    .in_3(demux_2_out_9), .in_1(not_1_out));
  _4_Bit_x_4_Bit_Comparator u_4_bit_x_4_bit_comparator_4 (
    .in_1(A2), .in_2(n4_bit_binary_subtractor_2_out_13), .in_3(n4_bit_binary_subtractor_2_out_12),
    .in_4(n4_bit_binary_subtractor_2_out_11), .in_5(B0), .in_6(B1), .in_7(B2), .in_8(B3),
    .out_11(n4_bit_x_4_bit_comparator_4_out_11));  // open: out_9, out_10
  _4_Bit_Binary_Subtractor u_4_bit_binary_subtractor_3 (
    .out_10(n4_bit_binary_subtractor_3_out_10), .out_11(n4_bit_binary_subtractor_3_out_11),
    .out_12(n4_bit_binary_subtractor_3_out_12), .out_13(n4_bit_binary_subtractor_3_out_13),
    .in_9(n4_bit_binary_subtractor_2_out_11), .in_8(demux_3_out_6), .in_7(n4_bit_binary_subtractor_2_out_12),
    .in_6(demux_3_out_7), .in_5(n4_bit_binary_subtractor_2_out_13), .in_4(demux_3_out_8), .in_2(A2),
    .in_3(demux_3_out_9), .in_1(not_1_out));
  not not_4 (Q1, n4_bit_x_4_bit_comparator_3_out_11);
  not not_5 (Q2, n4_bit_x_4_bit_comparator_4_out_11);

  // Notes on the sheet:
  //   DIVISION BY ZERO FLAG
endmodule

module _1_Bit_x_1_Bit_Comparator (
  input  in_1,
  input  in_2,
  output G,
  output E,
  output S
);

  wire not_1_out, not_2_out;

  not not_1 (not_1_out, in_2);
  not not_2 (not_2_out, in_1);
  and and_1 (G, in_1, not_1_out);
  and and_2 (S, not_2_out, in_2);
  nor nor_1 (E, G, S);
endmodule

module _4_Bit_x_4_Bit_Comparator (
  input  in_1,
  input  in_2,
  input  in_3,
  input  in_4,
  input  in_5,
  input  in_6,
  input  in_7,
  input  in_8,
  output out_9,
  output out_10,
  output out_11
);

  wire and_1_out, and_2_out, and_3_out, and_4_out, and_5_out, and_6_out, n1_bit_x_1_bit_comparator_1_e,
       n1_bit_x_1_bit_comparator_1_g, n1_bit_x_1_bit_comparator_1_s, n1_bit_x_1_bit_comparator_2_e,
       n1_bit_x_1_bit_comparator_2_g, n1_bit_x_1_bit_comparator_2_s, n1_bit_x_1_bit_comparator_3_e,
       n1_bit_x_1_bit_comparator_3_g, n1_bit_x_1_bit_comparator_3_s, n1_bit_x_1_bit_comparator_4_e,
       n1_bit_x_1_bit_comparator_4_g, n1_bit_x_1_bit_comparator_4_s;

  _1_Bit_x_1_Bit_Comparator u_1_bit_x_1_bit_comparator_1 (
    .in_1(in_1), .in_2(in_5), .G(n1_bit_x_1_bit_comparator_1_g), .E(n1_bit_x_1_bit_comparator_1_e),
    .S(n1_bit_x_1_bit_comparator_1_s));
  _1_Bit_x_1_Bit_Comparator u_1_bit_x_1_bit_comparator_2 (
    .in_1(in_2), .in_2(in_6), .G(n1_bit_x_1_bit_comparator_2_g), .E(n1_bit_x_1_bit_comparator_2_e),
    .S(n1_bit_x_1_bit_comparator_2_s));
  _1_Bit_x_1_Bit_Comparator u_1_bit_x_1_bit_comparator_3 (
    .in_1(in_3), .in_2(in_7), .G(n1_bit_x_1_bit_comparator_3_g), .E(n1_bit_x_1_bit_comparator_3_e),
    .S(n1_bit_x_1_bit_comparator_3_s));
  _1_Bit_x_1_Bit_Comparator u_1_bit_x_1_bit_comparator_4 (
    .in_1(in_4), .in_2(in_8), .G(n1_bit_x_1_bit_comparator_4_g), .E(n1_bit_x_1_bit_comparator_4_e),
    .S(n1_bit_x_1_bit_comparator_4_s));
  and and_1 (and_1_out, n1_bit_x_1_bit_comparator_3_g, n1_bit_x_1_bit_comparator_4_e);
  and and_2 (and_2_out, n1_bit_x_1_bit_comparator_2_g, n1_bit_x_1_bit_comparator_3_e, n1_bit_x_1_bit_comparator_4_e);
  and and_3 (and_3_out, n1_bit_x_1_bit_comparator_1_g, n1_bit_x_1_bit_comparator_2_e, n1_bit_x_1_bit_comparator_3_e, n1_bit_x_1_bit_comparator_4_e);
  and and_4 (and_4_out, n1_bit_x_1_bit_comparator_2_s, n1_bit_x_1_bit_comparator_3_e, n1_bit_x_1_bit_comparator_4_e);
  and and_5 (and_5_out, n1_bit_x_1_bit_comparator_3_s, n1_bit_x_1_bit_comparator_4_e);
  and and_6 (and_6_out, n1_bit_x_1_bit_comparator_4_e, n1_bit_x_1_bit_comparator_3_e, n1_bit_x_1_bit_comparator_2_e, n1_bit_x_1_bit_comparator_1_s);
  or or_1 (out_9, n1_bit_x_1_bit_comparator_4_g, and_1_out, and_2_out, and_3_out);
  and and_7 (out_10, n1_bit_x_1_bit_comparator_1_e, n1_bit_x_1_bit_comparator_2_e, n1_bit_x_1_bit_comparator_3_e, n1_bit_x_1_bit_comparator_4_e);
  or or_2 (out_11, and_6_out, and_4_out, and_5_out, n1_bit_x_1_bit_comparator_4_s);
endmodule
